// Digital circuit Circuit Diagram.dig as structural Verilog
module Circuit_Diagram (
  input  cs2,
  input  cs1,
  input  cs0,
  input  A0,
  input  B0,
  input  A1,
  input  B1,
  input  A2,
  input  B2,
  input  A3,
  input  B3,
  output S0,
  output S1,
  output S2,
  output S3,
  output S4,
  output ZeroFlag,
  output SignFlag,
  output CarryFlag,
  output OverflowFlag
);

  wire add_1_c_o, add_2_c_o, add_3_c_o, add_4_c_o, and_1_out, and_2_out, and_3_out, and_4_out, and_5_out,
       and_6_out, and_7_out, and_8_out, and_9_out, and_10_out, and_11_out, and_12_out, or_1_out, or_2_out,
       or_3_out, or_4_out, or_5_out, xor_1_out, xor_2_out, xor_3_out;

  xor xor_1 (xor_1_out, 1'b1, cs2);
  xor xor_2 (xor_2_out, cs0, xor_1_out);
  or or_1 (or_1_out, cs0, xor_1_out);
  and and_1 (and_1_out, cs1, xor_1_out);
  or or_2 (or_2_out, or_1_out, B0);
  and and_2 (and_2_out, add_1_c_o, xor_1_out);
  or or_3 (or_3_out, or_1_out, B1);
  and and_3 (and_3_out, add_2_c_o, xor_1_out);
  or or_4 (or_4_out, or_1_out, B2);
  and and_4 (and_4_out, add_3_c_o, xor_1_out);
  or or_5 (or_5_out, or_1_out, B3);
  and and_5 (and_5_out, A0, or_2_out);
  and and_6 (and_6_out, xor_2_out, B0);
  and and_7 (and_7_out, A1, or_3_out);
  and and_8 (and_8_out, xor_2_out, B1);
  and and_9 (and_9_out, A2, or_4_out);
  and and_10 (and_10_out, xor_2_out, B2);
  and and_11 (and_11_out, A3, or_5_out);
  and and_12 (and_12_out, xor_2_out, B3);
  Add add_1 (.a(and_5_out), .b(and_6_out), .c_i(and_1_out), .s(S0), .c_o(add_1_c_o));
  Add add_2 (.a(and_7_out), .b(and_8_out), .c_i(and_2_out), .s(S1), .c_o(add_2_c_o));
  Add add_3 (.a(and_9_out), .b(and_10_out), .c_i(and_3_out), .s(S2), .c_o(add_3_c_o));
  Add add_4 (.a(and_11_out), .b(and_12_out), .c_i(and_4_out), .s(S3), .c_o(add_4_c_o));
  xor xor_3 (xor_3_out, add_4_c_o, 1'b1);
  nor nor_1 (CarryFlag, xor_3_out, cs2);
  nor nor_2 (ZeroFlag, S0, S1, S2, S3);
  xor xor_4 (OverflowFlag, and_4_out, CarryFlag);

  assign S4 = CarryFlag;
  assign SignFlag = S3;
endmodule
