// Logisim project LogisimDemo.circ as structural Verilog: 1 circuit, main circuit main
module main (
  input  Cs2,
  input  Cs1,
  input  Cs0,
  input  B0,
  input  A0,
  input  B1,
  input  A1,
  input  B2,
  input  A2,
  input  B3,
  input  A3,
  output S0,
  output S1,
  output ZF,
  output S2,
  output SF,
  output S3,
  output CF,
  output OF
);

  wire adder_1_cout, adder_2_cout, adder_3_cout, and_1_out, and_2_out, and_3_out, and_4_out, and_5_out,
       and_6_out, and_7_out, and_8_out, and_9_out, and_10_out, and_11_out, and_12_out, not_1_out, or_1_out,
       or_2_out, or_3_out, or_4_out, xnor_1_out;

  not not_1 (not_1_out, Cs2);
  or or_1 (or_1_out, not_1_out, B0, Cs0);
  xnor xnor_1 (xnor_1_out, Cs2, Cs0);
  or or_2 (or_2_out, not_1_out, B1, Cs0);
  or or_3 (or_3_out, not_1_out, B2, Cs0);
  or or_4 (or_4_out, not_1_out, B3, Cs0);
  and and_1 (and_1_out, or_1_out, A0);
  and and_2 (and_2_out, xnor_1_out, B0);
  and and_3 (and_3_out, not_1_out, Cs1);
  and and_4 (and_4_out, or_2_out, A1);
  and and_5 (and_5_out, xnor_1_out, B1);
  and and_6 (and_6_out, not_1_out, adder_1_cout);
  and and_7 (and_7_out, or_3_out, A2);
  and and_8 (and_8_out, xnor_1_out, B2);
  and and_9 (and_9_out, not_1_out, adder_2_cout);
  and and_10 (and_10_out, or_4_out, A3);
  and and_11 (and_11_out, xnor_1_out, B3);
  and and_12 (and_12_out, not_1_out, adder_3_cout);
  Adder #(.width(1)) adder_1 (.a(and_1_out), .b(and_2_out), .out(S0), .cin(and_3_out), .cout(adder_1_cout));
  Adder #(.width(1)) adder_2 (.a(and_4_out), .b(and_5_out), .out(S1), .cin(and_6_out), .cout(adder_2_cout));
  Adder #(.width(1)) adder_3 (.a(and_7_out), .b(and_8_out), .out(S2), .cin(and_9_out), .cout(adder_3_cout));
  Adder #(.width(1)) adder_4 (.a(and_10_out), .b(and_11_out), .out(S3), .cin(and_12_out), .cout(CF));
  xor xor_1 (OF, CF, adder_3_cout);
  nor nor_1 (ZF, S0, S1, S2, S3);

  assign SF = S3;
endmodule
