// Digital circuit ALU_14_3_vl.dig as structural Verilog
module ALU_14_3_vl (
  input  A3,
  input  A2,
  input  A1,
  input  A0,
  input  B0,
  input  B1,
  input  B2,
  input  B3,
  input  CS0,
  input  CS2,
  input  CS1,
  output SignFlag,
  output OverflowFlag,
  output Z0,
  output Z3,
  output Z2,
  output Z1,
  output ZeroFlag,
  output CarryFlag
);

  wire _7404_1_pin5, _7404_1_pin6, _7408_1_pin3, _7408_1_pin6, _7408_1_pin8, _7408_1_pin11, _7421_1_pin4,
       _7421_1_pin5, _7421_1_pin6, _7421_1_pin8, _7421_1_pin10, _7421_1_pin12, _7421_1_pin13, _7483_1_pin2,
       _7483_1_pin6, _7483_1_pin9, _7486_1_pin3, _7486_1_pin6, _7486_1_pin8, _7486_1_pin11, _74157_1_pin4,
       _74157_1_pin7, _74157_1_pin9, _74157_1_pin12, _74157_2_pin4, _74157_2_pin7, _74157_2_pin9,
       _74157_2_pin12;

  _7408 _7408_1 (
    .pin1(A0), .pin2(B0), .pin3(_7408_1_pin3), .pin4(A1), .pin5(B1), .pin6(_7408_1_pin6), .pin7(1'b0),
    .pin8(_7408_1_pin8), .pin9(A2), .pin10(B2), .pin11(_7408_1_pin11), .pin12(A3), .pin13(B3), .pin14(1'b1));
  _7486 _7486_1 (
    .pin1(A0), .pin2(B0), .pin3(_7486_1_pin3), .pin4(A1), .pin5(B1), .pin6(_7486_1_pin6), .pin7(1'b0),
    .pin8(_7486_1_pin8), .pin9(A2), .pin10(B2), .pin11(_7486_1_pin11), .pin12(A3), .pin13(B3), .pin14(1'b1));
  _74157 _74157_1 (
    .pin1(CS0), .pin2(B0), .pin3(1'b0), .pin4(_74157_1_pin4), .pin5(B1), .pin6(1'b0), .pin7(_74157_1_pin7),
    .pin8(1'b0), .pin9(_74157_1_pin9), .pin10(1'b0), .pin11(B2), .pin12(_74157_1_pin12), .pin13(1'b0),
    .pin14(B3), .pin15(1'b0), .pin16(1'b1));
  _74157 _74157_2 (
    .pin1(CS0), .pin2(_7408_1_pin3), .pin3(_7486_1_pin3), .pin4(_74157_2_pin4), .pin5(_7408_1_pin6),
    .pin6(_7486_1_pin6), .pin7(_74157_2_pin7), .pin8(1'b0), .pin9(_74157_2_pin9), .pin10(_7486_1_pin8),
    .pin11(_7408_1_pin8), .pin12(_74157_2_pin12), .pin13(_7486_1_pin11), .pin14(_7408_1_pin11), .pin15(1'b0),
    .pin16(1'b1));
  _7421 _7421_1 (
    .pin1(A3), .pin2(_74157_1_pin12), .pin4(_7421_1_pin4), .pin5(_7421_1_pin5), .pin6(_7421_1_pin6),
    .pin7(1'b0), .pin8(_7421_1_pin8), .pin9(_7421_1_pin5), .pin10(_7421_1_pin10), .pin12(_7421_1_pin12),
    .pin13(_7421_1_pin13), .pin14(1'b1));  // open: pin3, pin11
  _7404 _7404_1 (
    .pin1(A3), .pin2(_7421_1_pin13), .pin3(A0), .pin5(_7404_1_pin5), .pin6(_7404_1_pin6), .pin7(1'b0),
    .pin8(_7421_1_pin5), .pin9(CS2), .pin10(_7421_1_pin4), .pin11(_7421_1_pin10), .pin12(_7421_1_pin12),
    .pin13(_74157_1_pin12), .pin14(1'b1));  // open: pin4
  _7483 _7483_1 (
    .pin1(A3), .pin2(_7483_1_pin2), .pin3(A2), .pin4(_74157_1_pin9), .pin5(1'b1), .pin6(_7483_1_pin6),
    .pin7(_74157_1_pin7), .pin8(A1), .pin9(_7483_1_pin9), .pin10(A0), .pin11(_74157_1_pin4), .pin12(1'b0),
    .pin13(CS1), .pin14(_7404_1_pin5), .pin15(_7421_1_pin10), .pin16(_74157_1_pin12));
  _7432 _7432_1 (
    .pin1(_7421_1_pin6), .pin2(_7421_1_pin8), .pin3(OverflowFlag), .pin4(OverflowFlag), .pin5(OverflowFlag),
    .pin7(1'b0), .pin9(1'b1), .pin10(1'b1), .pin12(1'b1), .pin13(1'b1), .pin14(1'b1));  // open: pin6, pin8, pin11
  _74157 _74157_3 (
    .pin1(CS2), .pin2(_7483_1_pin9), .pin3(_74157_2_pin4), .pin4(Z0), .pin5(_7483_1_pin6),
    .pin6(_74157_2_pin7), .pin7(Z1), .pin8(1'b0), .pin9(Z2), .pin10(_74157_2_pin9), .pin11(_7483_1_pin2),
    .pin12(SignFlag), .pin13(_74157_2_pin12), .pin14(_7421_1_pin10), .pin15(1'b0), .pin16(1'b1));
  _7425 _7425_1 (
    .pin1(_7483_1_pin9), .pin2(_7483_1_pin6), .pin4(_7483_1_pin2), .pin5(_7421_1_pin10), .pin6(ZeroFlag),
    .pin7(1'b0), .pin8(CarryFlag), .pin9(_7404_1_pin6), .pin10(CS2), .pin12(CS2), .pin13(CS2), .pin14(1'b1));  // open: pin3, pin11

  assign Z3 = SignFlag;
endmodule
