// Digital circuit ALU.dig as structural Verilog
module ALU (
  input  [15:0] A_in,
  input  [15:0] B_in,
  input  A_sign,
  input  B_sign,
  output S,
  output [15:0] N
);

  wire decoder_1_out_1, decoder_1_out_2, decoder_1_out_3, or_1_out;
  wire [15:0] add_1_s, bitextender_1_out, bitextender_2_out, bitextender_3_out, bitextender_4_out, xor_1_out,
       xor_2_out, xor_3_out;

  Decoder #(.Selector_Bits(2)) decoder_1 (
    .sel({B_sign, A_sign}), .out_1(decoder_1_out_1), .out_2(decoder_1_out_2), .out_3(decoder_1_out_3));  // open: out_0
  or or_1 (or_1_out, decoder_1_out_1, decoder_1_out_2);
  BitExtender #(.inputBits(1)) bitextender_1 (.in(decoder_1_out_1), .out(bitextender_1_out));
  BitExtender #(.inputBits(1)) bitextender_2 (.in(decoder_1_out_2), .out(bitextender_2_out));
  assign xor_1_out = A_in ^ bitextender_1_out;  // XOr xor_1, 16 bits wide
  assign xor_2_out = bitextender_2_out ^ B_in;  // XOr xor_2, 16 bits wide
  Add #(.Bits(16)) add_1 (.a(xor_1_out), .b(xor_2_out), .c_i(or_1_out), .s(add_1_s));  // open: c_o
  BitExtender #(.inputBits(1)) bitextender_3 (.in(add_1_s[15]), .out(bitextender_3_out));
  or or_2 (S, add_1_s[15], decoder_1_out_3);
  assign xor_3_out = add_1_s ^ bitextender_3_out;  // XOr xor_3, 16 bits wide
  BitExtender #(.inputBits(1)) bitextender_4 (.in(1'b0), .out(bitextender_4_out));
  Add #(.Bits(16)) add_2 (.a(xor_3_out), .b(bitextender_4_out), .c_i(add_1_s[15]), .s(N));  // open: c_o
endmodule
