// Digital circuit exponent_sorter.dig as structural Verilog
module exponent_sorter (
  input  [15:0] N_a,
  input  [15:0] N_b,
  output [15:0] LE,
  output [15:0] SE
);

  wire comparator_1_lt;

  Comparator #(.Bits(4)) comparator_1 (.a(N_a[14:11]), .b(N_b[14:11]), .lt(comparator_1_lt));  // open: gt, eq
  Multiplexer #(.Bits(16)) multiplexer_1 (.sel(comparator_1_lt), .in_0(N_a), .in_1(N_b), .out(LE));
  Multiplexer #(.Bits(16)) multiplexer_2 (.sel(comparator_1_lt), .in_0(N_b), .in_1(N_a), .out(SE));
endmodule
