// Digital circuit floating_point_decoder.dig as structural Verilog
module floating_point_decoder (
  input  [15:0] N_in,
  output S,
  output [3:0] E,
  output [15:0] M
);

  or or_1 (M[13], N_in[11], N_in[12], N_in[13], N_in[14]);

  assign E = N_in[14:11];
  assign {M[15:14], M[12:0]} = {2'b00, N_in[10:0], 2'b00};
  assign S = N_in[15];
endmodule
