// Digital circuit input_processing.dig as structural Verilog
module input_processing (
  input  [15:0] I_1,
  input  [15:0] I_2,
  output [15:0] R,
  output OF,
  output UF
);

  wire floating_point_decoder_1_s, floating_point_decoder_2_s, sum_calc_1_p3, sum_calc_1_p4, sum_calc_1_p5;
  wire [3:0] floating_point_decoder_1_e, floating_point_decoder_2_e, sub_1_s;
  wire [4:4] sub_1_c_o;
  wire [15:0] alu_1_n, barrelshifter_1_out, exponent_sorter_1_le, exponent_sorter_1_se,
       floating_point_decoder_1_m, floating_point_decoder_2_m;

  exponent_sorter exponent_sorter_1 (.N_a(I_1), .N_b(I_2), .LE(exponent_sorter_1_le), .SE(exponent_sorter_1_se));
  floating_point_decoder floating_point_decoder_1 (
    .N_in(exponent_sorter_1_le), .S(floating_point_decoder_1_s), .E(floating_point_decoder_1_e),
    .M(floating_point_decoder_1_m));
  floating_point_decoder floating_point_decoder_2 (
    .N_in(exponent_sorter_1_se), .S(floating_point_decoder_2_s), .E(floating_point_decoder_2_e),
    .M(floating_point_decoder_2_m));
  Sub #(.Bits(4)) sub_1 (
    .a(floating_point_decoder_1_e), .b(floating_point_decoder_2_e), .c_i(1'b0), .s(sub_1_s),
    .c_o(sub_1_c_o[4]));
  BarrelShifter #(.Bits(16), .direction("right")) barrelshifter_1 (
    .in(floating_point_decoder_2_m), .shift({sub_1_c_o[4], sub_1_s}), .out(barrelshifter_1_out));
  ALU alu_1 (
    .A_sign(floating_point_decoder_1_s), .A_in(floating_point_decoder_1_m),
    .B_sign(floating_point_decoder_2_s), .B_in(barrelshifter_1_out), .N(alu_1_n), .S(R[15]));
  // sum_calc sum_calc_1: pin names not known; wires that end beside it: alu_1_n, R[10:0], sum_calc_1_p3, sum_calc_1_p4, sum_calc_1_p5
  // normalizer normalizer_1: pin names not known; wires that end beside it: floating_point_decoder_1_e, sum_calc_1_p3, sum_calc_1_p4, sum_calc_1_p5, R[14:11], OF, UF
  // Pins of 1 and 16 bits meet at R
endmodule
