// Digital circuit normalizer.dig as structural Verilog
module normalizer (
  input  C,
  input  [3:0] ME,
  input  [3:0] Sh,
  input  NZ,
  output OF,
  output [3:0] E,
  output UF
);

  wire add_1_c_o, and_1_out, nor_1_out, or_2_out, sub_1_c_o;
  wire [3:0] add_1_s;

  Add #(.Bits(4)) add_1 (.a(ME), .b(4'b0000), .c_i(C), .s(add_1_s), .c_o(add_1_c_o));
  or or_1 (OF, and_1_out, add_1_c_o);
  and and_1 (and_1_out, add_1_s[1], add_1_s[0], add_1_s[2], add_1_s[3]);
  Sub #(.Bits(4)) sub_1 (.a(add_1_s), .b(Sh), .c_i(1'b0), .s(E), .c_o(sub_1_c_o));
  or or_2 (or_2_out, nor_1_out, sub_1_c_o);
  nor nor_1 (nor_1_out, E[1], E[0], E[2], E[3]);
  and and_2 (UF, or_2_out, NZ);
endmodule
