// Digital circuit sum_calc.dig as structural Verilog
module sum_calc (
  input  [15:0] N,
  output [10:0] Ma,
  output [4:0] Sh,
  output NZ,
  output C
);

  wire [3:0] priorityencoder_1_num;
  wire [10:0] _1to11_out;
  wire [15:0] Lt_out, Rt_out;

  BarrelShifter #(.Bits(16), .direction("right")) Rt (.in(N), .shift({4'b0000, N[14]}), .out(Rt_out));
  PriorityEncoder #(.Selector_Bits(4)) priorityencoder_1 (
    .in0(Rt_out[0]), .in1(Rt_out[1]), .in2(Rt_out[2]), .in3(Rt_out[3]), .in4(Rt_out[4]), .in5(Rt_out[5]),
    .in6(Rt_out[6]), .in7(Rt_out[7]), .in8(Rt_out[8]), .in9(Rt_out[9]), .in10(Rt_out[10]), .in11(Rt_out[11]),
    .in12(Rt_out[12]), .in13(Rt_out[13]), .in14(1'b0), .in15(1'b0), .num(priorityencoder_1_num), .any(NZ));
  Sub #(.Bits(4)) sub_1 (.a(4'b1101), .b(priorityencoder_1_num), .c_i(1'b0), .s(Sh[3:0]));  // open: c_o
  BarrelShifter #(.Bits(16)) Lt (.in(N), .shift({1'b0, Sh[3:0]}), .out(Lt_out));
  BitExtender #(.inputBits(1), .outputBits(11)) _1to11 (.in(NZ), .out(_1to11_out));
  assign Ma = Lt_out[12:2] & _1to11_out;  // And and_1, 11 bits wide
  // Pins of 4 and 5 bits meet at Sh

  assign C = N[14];
endmodule
