// Logisim project initial circuit.circ as structural Verilog: 17 circuits, main circuit demo
module demo (
  input  [15:0] in_1,
  input  [15:0] in_2,
  output [15:0] out_3,
  output underflow,
  output overflow
);

  final_circuit final_circuit_1 (
    .input_fp_1(in_1), .input_fp_2(in_2), .sum(out_3), .underflow(underflow), .overflow(overflow));
endmodule

// ALU
module ALU_Add_16___sign_bit (
  input  [15:0] input_1,
  input  sign_1,
  input  sign_2,
  input  [15:0] input_2,
  output [15:0] \output ,
  output output_sign
);

  wire and_1_out, and_2_out, and_3_out, not_1_out, xor_1_out;
  wire [15:0] adder_1_out, bit_extender_1_out, bit_extender_2_out, bit_extender_3_out, xor_2_out, xor_3_out,
       xor_4_out;

  xor xor_1 (xor_1_out, sign_1, sign_2);
  and and_1 (and_1_out, sign_1, xor_1_out);
  not not_1 (not_1_out, xor_1_out);
  and and_2 (and_2_out, xor_1_out, sign_2);
  assign bit_extender_1_out = {{15{and_1_out}}, and_1_out};  // Bit_Extender bit_extender_1
  and and_3 (and_3_out, not_1_out, sign_2);
  assign bit_extender_2_out = {{15{and_2_out}}, and_2_out};  // Bit_Extender bit_extender_2
  assign xor_2_out = input_1 ^ bit_extender_1_out;  // XOR_Gate xor_2, 16 bits wide
  assign xor_3_out = bit_extender_2_out ^ input_2;  // XOR_Gate xor_3, 16 bits wide
  Adder #(.width(16)) adder_1 (.a(xor_2_out), .b(xor_3_out), .out(adder_1_out), .cin(xor_1_out));  // open: cout
  assign bit_extender_3_out = {{15{adder_1_out[15]}}, adder_1_out[15]};  // Bit_Extender bit_extender_3
  or or_1 (output_sign, adder_1_out[15], and_3_out);
  assign xor_4_out = adder_1_out ^ bit_extender_3_out;  // XOR_Gate xor_4, 16 bits wide
  Adder #(.width(16)) adder_2 (.a({16{1'b0}}), .b(xor_4_out), .out(\output ), .cin(adder_1_out[15]));  // open: cout
endmodule

// inut sorter
module input_sorter (
  input  [15:0] in_1,
  input  [15:0] in_2,
  output [15:0] max_number,
  output [15:0] min_number
);

  wire comparator_1_gt;

  Comparator #(.width(4), .mode("unsigned")) comparator_1 (
    .a(in_1[14:11]), .b(in_2[14:11]), .gt(comparator_1_gt));  // open: eq, lt
  Multiplexer #(.width(16), .disabled(0), .enable("false")) multiplexer_1 (
    .in0(in_2), .in1(in_1), .out(max_number), .sel(comparator_1_gt));
  Multiplexer #(.width(16), .disabled(0), .enable("false")) multiplexer_2 (
    .in0(in_1), .in1(in_2), .out(min_number), .sel(comparator_1_gt));
endmodule

module final_circuit (
  input  [15:0] input_fp_1,
  input  [15:0] input_fp_2,
  output [15:0] sum,
  output underflow,
  output overflow
);

  wire adder_1_cout, alu_add_16_sign_bit_1_output_sign, and_1_out, floating_point_decoder_1_sign, sign_mn;
  wire [3:0] adder_1_out, bit_extender_1_out, exponent_mx, floating_point_decoder_2_exponent,
       subtractor_1_out;
  wire [15:0] alu_add_16_sign_bit_1_output, floating_point_decoder_1_mantissa,
       floating_point_decoder_2_mantissa, input_sorter_1_max_number, input_sorter_1_min_number,
       shifter_1_out, shifter_2_out;

  input_sorter input_sorter_1 (
    .in_1(input_fp_1), .in_2(input_fp_2), .max_number(input_sorter_1_max_number),
    .min_number(input_sorter_1_min_number));
  floating_point_decoder floating_point_decoder_1 (
    .FLOATING_POINT(input_sorter_1_max_number), .MANTISSA(floating_point_decoder_1_mantissa),
    .SIGN(floating_point_decoder_1_sign), .EXPONENT(exponent_mx));
  floating_point_decoder floating_point_decoder_2 (
    .FLOATING_POINT(input_sorter_1_min_number), .MANTISSA(floating_point_decoder_2_mantissa), .SIGN(sign_mn),
    .EXPONENT(floating_point_decoder_2_exponent));
  Subtractor #(.width(4)) subtractor_1 (
    .a(exponent_mx), .b(floating_point_decoder_2_exponent), .out(subtractor_1_out), .bin(1'b0));  // open: bout
  Shifter #(.width(16), .shift("lr")) shifter_1 (
    .in(floating_point_decoder_2_mantissa), .\dist (subtractor_1_out), .out(shifter_1_out));
  ALU_Add_16___sign_bit alu_add_16_sign_bit_1 (
    .input_1(floating_point_decoder_1_mantissa), .sign_1(floating_point_decoder_1_sign), .sign_2(sign_mn),
    .input_2(shifter_1_out), .\output (alu_add_16_sign_bit_1_output),
    .output_sign(alu_add_16_sign_bit_1_output_sign));
  assign bit_extender_1_out = {{3{1'b0}}, alu_add_16_sign_bit_1_output[14]};  // Bit_Extender bit_extender_1
  Adder #(.width(4)) adder_1 (
    .a(4'b0000), .b(exponent_mx), .out(adder_1_out), .cin(alu_add_16_sign_bit_1_output[14]),
    .cout(adder_1_cout));
  Shifter #(.width(16), .shift("lr")) shifter_2 (
    .in(alu_add_16_sign_bit_1_output), .\dist (bit_extender_1_out), .out(shifter_2_out));
  and and_1 (and_1_out, adder_1_out[0], adder_1_out[1], adder_1_out[2], adder_1_out[3]);
  or or_1 (overflow, and_1_out, adder_1_cout);
  normalizer normalizer_1 (
    .mantissa_in_13_12_11_10(shifter_2_out), .sign(alu_add_16_sign_bit_1_output_sign),
    .exponent(adder_1_out), .floating_point(sum), .underflow(underflow));

  // Notes on the sheet:
  //   maximum number
  //   minimum number
  //   sign
  //   exponent
  //   answer = [13].[12][11][10]..
endmodule

module normalizer (
  input  [15:0] mantissa_in_13_12_11_10,
  input  sign,
  input  [3:0] exponent,
  output [15:0] floating_point,
  output underflow
);

  wire nonzero_output, nor_1_out, or_1_out, subtractor_2_bout, zero_output;
  wire [3:0] priority_encoder_1_out, subtractor_1_out, subtractor_2_out;
  wire [15:0] bit_extender_1_out, shifter_1_out;

  Priority_Encoder #(.select(4), .disabled(0)) priority_encoder_1 (
    .in0(mantissa_in_13_12_11_10[0]), .in1(mantissa_in_13_12_11_10[1]), .in2(mantissa_in_13_12_11_10[2]),
    .in3(mantissa_in_13_12_11_10[3]), .in4(mantissa_in_13_12_11_10[4]), .in5(mantissa_in_13_12_11_10[5]),
    .in6(mantissa_in_13_12_11_10[6]), .in7(mantissa_in_13_12_11_10[7]), .in8(mantissa_in_13_12_11_10[8]),
    .in9(mantissa_in_13_12_11_10[9]), .in10(mantissa_in_13_12_11_10[10]), .in11(mantissa_in_13_12_11_10[11]),
    .in12(mantissa_in_13_12_11_10[12]), .in13(mantissa_in_13_12_11_10[13]), .in14(1'b0), .in15(1'b0),
    .out(priority_encoder_1_out), .gs(nonzero_output), .en_out(zero_output), .en_in(1'b1));
  Subtractor #(.width(4)) subtractor_1 (
    .a(4'b1101), .b(priority_encoder_1_out), .out(subtractor_1_out), .bin(1'b0));  // open: bout
  Shifter #(.width(16)) shifter_1 (.in(mantissa_in_13_12_11_10), .\dist (subtractor_1_out), .out(shifter_1_out));
  Subtractor #(.width(4)) subtractor_2 (
    .a(exponent), .b(subtractor_1_out), .out(subtractor_2_out), .bin(1'b0), .bout(subtractor_2_bout));
  nor nor_1 (nor_1_out, subtractor_2_out[1], subtractor_2_out[0], subtractor_2_out[2], subtractor_2_out[3]);
  or or_1 (or_1_out, nor_1_out, subtractor_2_bout);
  assign bit_extender_1_out = {{15{nonzero_output}}, nonzero_output};  // Bit_Extender bit_extender_1
  and and_1 (underflow, nonzero_output, or_1_out);
  assign floating_point = bit_extender_1_out & {sign, subtractor_2_out, shifter_1_out[12:2]};  // AND_Gate and_2, 16 bits wide

  // Notes on the sheet:
  //   left  shfit count
  //   answer = [13].[12][11][10]..
  //   underflow
endmodule

// Floating Point Decoder
module floating_point_decoder (
  input  [15:0] FLOATING_POINT,
  output [15:0] MANTISSA,
  output SIGN,
  output [3:0] EXPONENT
);


  assign EXPONENT = FLOATING_POINT[14:11];
  assign MANTISSA = {3'b001, FLOATING_POINT[10:0], 2'b00};
  assign SIGN = FLOATING_POINT[15];
endmodule

module input_sorter_ic (
  input  [15:0] input_0,
  input  [15:0] input_1,
  output [15:0] max_number,
  output [15:0] min_number
);

  wire dip_7485_1_p5;

  // DIP_7485 dip_7485_1: pin names not known; wires that end beside it: input_1[14], 1'b0, 1'b1, 1'b0, dip_7485_1_p5, input_0[14], input_1[13], input_0[13], input_0[12], input_1[12], input_0[11], input_1[11]
  _16_2_line_mux_ic u_16_2_line_mux_ic_1 (
    .input_0(input_1), .input_1(input_0), .selection(dip_7485_1_p5), .out_4(max_number));
  _16_2_line_mux_ic u_16_2_line_mux_ic_2 (
    .input_0(input_0), .input_1(input_1), .selection(dip_7485_1_p5), .out_4(min_number));

  // Other names for the same wires on the sheet: A1 = input_0[11]; A2 = input_0[12]; A3 = input_0[13];
  //   A4 = input_0[14]; B1 = input_1[11]; B2 = input_1[12]; B3 = input_1[13]; B4 = input_1[14]
endmodule

module _16_2_line_mux_ic (
  input  [15:0] input_0,
  input  [15:0] input_1,
  input  selection,
  output [15:0] out_4
);

  // DIP_74157 dip_74157_1: pin names not known; wires that end beside it: selection, input_0[0], input_1[0], out_4[0], input_0[1], input_1[1], out_4[1], 1'b0, input_0[3], input_1[3], out_4[3], input_0[2], input_1[2]
  // DIP_74157 dip_74157_2: pin names not known; wires that end beside it: selection, input_0[4], input_1[4], out_4[4], input_0[5], input_1[5], out_4[2], 1'b0, input_0[7], input_1[7], out_4[7], input_0[6]
  // DIP_74157 dip_74157_3: pin names not known; wires that end beside it: out_4[5], selection, input_0[8], input_1[8], out_4[8], input_0[9], input_1[9], input_1[6], out_4[6], 1'b0, input_0[11], input_1[11], out_4[11], input_0[10]
  // DIP_74157 dip_74157_4: pin names not known; wires that end beside it: out_4[9], selection, input_0[12], input_1[12], out_4[12], input_0[13], input_1[13], out_4[13], input_1[10], out_4[10], 1'b0, input_0[15], input_1[15], out_4[15], input_0[14], input_1[14], out_4[14]

  // Other names for the same wires on the sheet: A1 = input_0[0]; A2 = input_0[1]; A3 = input_0[2]; A4 = input_0[3];
  //   A5 = input_0[4]; A6 = input_0[5]; A7 = input_0[6]; A8 = input_0[7]; A9 = input_0[8]; A10 = input_0[9];
  //   A11 = input_0[10]; A12 = input_0[11]; A13 = input_0[12]; A14 = input_0[13]; A15 = input_0[14];
  //   A16 = input_0[15]; B1 = input_1[0]; B2 = input_1[1]; B3 = input_1[2]; B4 = input_1[3]; B5 = input_1[4];
  //   B6 = input_1[5]; B7 = input_1[6]; B8 = input_1[7]; B9 = input_1[8]; B10 = input_1[9]; B11 = input_1[10];
  //   B12 = input_1[11]; B13 = input_1[12]; B14 = input_1[13]; B15 = input_1[14]; B16 = input_1[15]; S0 = selection
endmodule

module final_circuit_ic (
  input  [15:0] input_fp_1,
  input  [15:0] input_fp_2,
  output [15:0] sum,
  output underflow,
  output overflow
);

  wire _7429_out, adder_4_bit_ic_1_out_5, answer_sign, dip_7421_1_p5, dip_7421_1_p7,
       floating_point_decoder_1_sign, nonzero_output, sign_mn, subtractor_ic_3_out_5, zero_output;
  wire [1:0] dip_7421_1_p11;
  wire [3:0] adder_4_bit_ic_1_out_4, bit_extender_1_out, exponent_mx, floating_point_decoder_2_exponent,
       priority_encoder_1_out, subtractor_ic_1_out_4, subtractor_ic_2_out_4;
  wire [14:0] shifter_3_out_2;
  wire [15:0] alu_ic_1_output, bit_extender_2_out, floating_point_decoder_1_mantissa,
       floating_point_decoder_2_mantissa, input_sorter_ic_1_max_number, input_sorter_ic_1_min_number,
       shifter_1_out, shifter_2_out, shifter_3_out;

  input_sorter_ic input_sorter_ic_1 (
    .input_0(input_fp_1), .input_1(input_fp_2), .max_number(input_sorter_ic_1_max_number),
    .min_number(input_sorter_ic_1_min_number));
  floating_point_decoder floating_point_decoder_1 (
    .FLOATING_POINT(input_sorter_ic_1_max_number), .MANTISSA(floating_point_decoder_1_mantissa),
    .SIGN(floating_point_decoder_1_sign), .EXPONENT(exponent_mx));
  floating_point_decoder floating_point_decoder_2 (
    .FLOATING_POINT(input_sorter_ic_1_min_number), .MANTISSA(floating_point_decoder_2_mantissa),
    .SIGN(sign_mn), .EXPONENT(floating_point_decoder_2_exponent));
  subtractor_ic subtractor_ic_1 (
    .in_2(exponent_mx), .in_3(floating_point_decoder_2_exponent), .out_4(subtractor_ic_1_out_4), .in_1(1'b0));  // open: out_5
  Shifter #(.width(16), .shift("lr")) shifter_1 (
    .in(floating_point_decoder_2_mantissa), .\dist (subtractor_ic_1_out_4), .out(shifter_1_out));
  ALU_ic alu_ic_1 (
    .input_1(floating_point_decoder_1_mantissa), .sign_1(floating_point_decoder_1_sign), .sign_2(sign_mn),
    .input_2(shifter_1_out), .\output (alu_ic_1_output), .output_sign(answer_sign));
  adder_4_bit_ic adder_4_bit_ic_1 (
    .input_1(4'b0000), .input_2(exponent_mx), .Cin(alu_ic_1_output[14]), .out_5(adder_4_bit_ic_1_out_5),
    .out_4(adder_4_bit_ic_1_out_4));
  assign bit_extender_1_out = {{3{1'b0}}, alu_ic_1_output[14]};  // Bit_Extender bit_extender_1
  // DIP_7421 dip_7421_1: pin names not known; wires that end beside it: adder_4_bit_ic_1_out_4[0], adder_4_bit_ic_1_out_4[1], adder_4_bit_ic_1_out_4[3], adder_4_bit_ic_1_out_4[2], dip_7421_1_p5, nonzero_output, dip_7421_1_p7, 1'b1, 1'b1, underflow, dip_7421_1_p11, 2'b00
  Shifter #(.width(16), .shift("lr")) shifter_2 (
    .in(alu_ic_1_output), .\dist (bit_extender_1_out), .out(shifter_2_out));
  subtractor_ic subtractor_ic_2 (
    .in_2(4'b1101), .in_3(priority_encoder_1_out), .out_4(subtractor_ic_2_out_4), .in_1(1'b0));  // open: out_5
  Priority_Encoder #(.select(4), .disabled(0)) priority_encoder_1 (
    .in0(shifter_2_out[0]), .in1(shifter_2_out[1]), .in2(shifter_2_out[2]), .in3(shifter_2_out[3]),
    .in4(shifter_2_out[4]), .in5(shifter_2_out[5]), .in6(shifter_2_out[6]), .in7(shifter_2_out[7]),
    .in8(shifter_2_out[8]), .in9(shifter_2_out[9]), .in10(shifter_2_out[10]), .in11(shifter_2_out[11]),
    .in12(shifter_2_out[12]), .in13(shifter_2_out[13]), .in14(dip_7421_1_p11[0]), .in15(dip_7421_1_p11[1]),
    .out(priority_encoder_1_out), .gs(nonzero_output), .en_out(zero_output), .en_in(1'b1));
  Shifter #(.width(16)) shifter_3 (
    .in(shifter_2_out), .\dist (subtractor_ic_2_out_4),
    .out({shifter_3_out[15:13], shifter_3_out_2[10:0], shifter_3_out[1:0]}));
  subtractor_ic subtractor_ic_3 (
    .in_2(adder_4_bit_ic_1_out_4), .in_3(subtractor_ic_2_out_4), .out_4(shifter_3_out_2[14:11]), .in_1(1'b0),
    .out_5(subtractor_ic_3_out_5));
  nor _7429 (_7429_out, shifter_3_out_2[11], shifter_3_out_2[12], shifter_3_out_2[14], shifter_3_out_2[13]);
  // DIP_7432 dip_7432_1: pin names not known; wires that end beside it: _7429_out, subtractor_ic_3_out_5, dip_7421_1_p7, adder_4_bit_ic_1_out_5, dip_7421_1_p5, overflow
  assign bit_extender_2_out = {{15{nonzero_output}}, nonzero_output};  // Bit_Extender bit_extender_2
  and_16_line_ic and_16_line_ic_1 (
    .input_1(bit_extender_2_out), .input_2({answer_sign, shifter_3_out_2}), .\output (sum));

  // Notes on the sheet:
  //   max_expo - min_expo
  //   exponent
  //   left  shfit count
endmodule

// -
module subtractor_ic (
  input  in_1,
  input  [3:0] in_2,
  input  [3:0] in_3,
  output [3:0] out_4,
  output out_5
);

  DIP_74181 dip_74181_1 (
    .S1(1'b0), .S2(1'b1), .S3(1'b1), .S4(1'b0), .B4(in_3[3]), .A4(in_2[3]), .B3(in_3[2]), .A3(in_2[2]),
    .B2(in_3[1]), .A2(in_2[1]), .B1(in_3[0]), .A1(in_2[0]), .M(1'b0), .CIN(in_1), .COUT(out_5),
    .Y4(out_4[3]), .Y3(out_4[2]), .Y2(out_4[1]), .Y1(out_4[0]));  // open: G, P, EQ
endmodule

// 74181
module DIP_74181 (
  input  S1,
  input  S2,
  input  S3,
  input  S4,
  input  B4,
  input  A4,
  input  B3,
  input  A3,
  input  B2,
  input  A2,
  input  B1,
  input  A1,
  input  M,
  input  CIN,
  output G,
  output COUT,
  output P,
  output Y4,
  output Y3,
  output EQ,
  output Y2,
  output Y1
);

  wire and_1_out, and_2_out, and_3_out, and_4_out, and_5_out, and_6_out, and_7_out, and_8_out, and_9_out,
       and_10_out, and_11_out, and_12_out, and_13_out, and_14_out, and_15_out, and_16_out, and_17_out,
       and_18_out, and_19_out, and_20_out, and_21_out, and_22_out, and_23_out, and_24_out, and_25_out,
       and_26_out, and_27_out, and_28_out, buffer_1_out, buffer_2_out, buffer_3_out, buffer_4_out,
       buffer_5_out, nand_1_out, nand_3_out, nor_1_out, nor_2_out, nor_3_out, nor_4_out, nor_5_out,
       nor_6_out, nor_7_out, nor_8_out, nor_10_out, nor_11_out, nor_12_out, not_1_out, not_2_out, not_3_out,
       not_4_out, not_5_out, xor_1_out, xor_2_out, xor_3_out, xor_4_out;

  not not_1 (not_1_out, B4);
  not not_2 (not_2_out, B3);
  not not_3 (not_3_out, B2);
  not not_4 (not_4_out, B1);
  not not_5 (not_5_out, M);
  and and_1 (and_1_out, B4, S1, A4);
  and and_2 (and_2_out, A4, S2, not_1_out);
  and and_3 (and_3_out, not_1_out, S3);
  and and_4 (and_4_out, S4, B4);
  buf buffer_1 (buffer_1_out, A4);
  and and_5 (and_5_out, B3, S1, A3);
  and and_6 (and_6_out, A3, S2, not_2_out);
  and and_7 (and_7_out, not_2_out, S3);
  and and_8 (and_8_out, S4, B3);
  buf buffer_2 (buffer_2_out, A3);
  and and_9 (and_9_out, B2, S1, A2);
  and and_10 (and_10_out, A2, S2, not_3_out);
  and and_11 (and_11_out, not_3_out, S3);
  and and_12 (and_12_out, S4, B2);
  buf buffer_3 (buffer_3_out, A2);
  and and_13 (and_13_out, B1, S1, A1);
  and and_14 (and_14_out, A1, S2, not_4_out);
  and and_15 (and_15_out, not_4_out, S3);
  and and_16 (and_16_out, S4, B1);
  buf buffer_4 (buffer_4_out, A1);
  nor nor_1 (nor_1_out, and_1_out, and_2_out);
  nor nor_2 (nor_2_out, and_3_out, and_4_out, buffer_1_out);
  nor nor_3 (nor_3_out, and_5_out, and_6_out);
  nor nor_4 (nor_4_out, and_7_out, and_8_out, buffer_2_out);
  nor nor_5 (nor_5_out, and_9_out, and_10_out);
  nor nor_6 (nor_6_out, and_11_out, and_12_out, buffer_3_out);
  nor nor_7 (nor_7_out, and_13_out, and_14_out);
  nor nor_8 (nor_8_out, and_15_out, and_16_out, buffer_4_out);
  xor xor_1 (xor_1_out, nor_1_out, nor_2_out);
  xor xor_2 (xor_2_out, nor_3_out, nor_4_out);
  xor xor_3 (xor_3_out, nor_5_out, nor_6_out);
  xor xor_4 (xor_4_out, nor_7_out, nor_8_out);
  buf buffer_5 (buffer_5_out, nor_2_out);
  and and_17 (and_17_out, nor_1_out, nor_4_out);
  and and_18 (and_18_out, nor_1_out, nor_3_out, nor_6_out);
  and and_19 (and_19_out, nor_1_out, nor_3_out, nor_5_out, nor_8_out);
  nand nand_1 (nand_1_out, nor_1_out, nor_3_out, nor_5_out, nor_7_out, CIN);
  nand nand_2 (P, nor_1_out, nor_3_out, nor_5_out, nor_7_out);
  and and_20 (and_20_out, CIN, nor_7_out, nor_5_out, nor_3_out, not_5_out);
  and and_21 (and_21_out, nor_5_out, nor_3_out, nor_8_out, not_5_out);
  and and_22 (and_22_out, nor_3_out, nor_6_out, not_5_out);
  and and_23 (and_23_out, nor_4_out, not_5_out);
  and and_24 (and_24_out, CIN, nor_7_out, nor_5_out, not_5_out);
  and and_25 (and_25_out, nor_5_out, nor_8_out, not_5_out);
  and and_26 (and_26_out, nor_6_out, not_5_out);
  and and_27 (and_27_out, CIN, nor_7_out, not_5_out);
  and and_28 (and_28_out, nor_8_out, not_5_out);
  nand nand_3 (nand_3_out, CIN, not_5_out);
  nor nor_9 (G, buffer_5_out, and_17_out, and_18_out, and_19_out);
  nor nor_10 (nor_10_out, and_20_out, and_21_out, and_22_out, and_23_out);
  nor nor_11 (nor_11_out, and_24_out, and_25_out, and_26_out);
  nor nor_12 (nor_12_out, and_27_out, and_28_out);
  nand nand_4 (COUT, G, nand_1_out);
  xor xor_5 (Y4, xor_1_out, nor_10_out);
  xor xor_6 (Y3, xor_2_out, nor_11_out);
  xor xor_7 (Y2, xor_3_out, nor_12_out);
  xor xor_8 (Y1, xor_4_out, nand_3_out);
  and and_29 (EQ, Y3, Y4, Y1, Y2);
endmodule

// ALU
module ALU_ic (
  input  [15:0] input_1,
  input  sign_1,
  input  sign_2,
  input  [15:0] input_2,
  output [15:0] \output ,
  output output_sign
);

  wire dip_7408_1_p3, dip_7408_1_p6, dip_7408_1_p9, dip_7486_1_p3, dip_7486_1_p6;
  wire [15:0] adder_16_bit_ic_1_out_4, bit_extender_1_out, bit_extender_2_out, bit_extender_3_out,
       xor_16_line_ic_1_output, xor_16_line_ic_2_output, xor_16_line_ic_3_output;

  // DIP_7486 dip_7486_1: pin names not known; wires that end beside it: sign_1, sign_2, dip_7486_1_p3, dip_7486_1_p3, 1'b1, dip_7486_1_p6
  // DIP_7408 dip_7408_1: pin names not known; wires that end beside it: sign_1, dip_7486_1_p3, dip_7408_1_p3, dip_7486_1_p3, sign_2, dip_7408_1_p6, dip_7486_1_p6, sign_2, dip_7408_1_p9
  assign bit_extender_1_out = {{15{dip_7408_1_p3}}, dip_7408_1_p3};  // Bit_Extender bit_extender_1
  assign bit_extender_2_out = {{15{dip_7408_1_p6}}, dip_7408_1_p6};  // Bit_Extender bit_extender_2
  xor_16_line_ic xor_16_line_ic_1 (.input_1(input_1), .input_2(bit_extender_1_out), .\output (xor_16_line_ic_1_output));
  xor_16_line_ic xor_16_line_ic_2 (.input_1(bit_extender_2_out), .input_2(input_2), .\output (xor_16_line_ic_2_output));
  adder_16_bit_ic adder_16_bit_ic_1 (
    .input_1(xor_16_line_ic_1_output), .input_2(xor_16_line_ic_2_output), .Cin(dip_7486_1_p3),
    .out_4(adder_16_bit_ic_1_out_4));  // open: out_5
  assign bit_extender_3_out = {{15{adder_16_bit_ic_1_out_4[15]}}, adder_16_bit_ic_1_out_4[15]};  // Bit_Extender bit_extender_3
  // DIP_7432 dip_7432_1: pin names not known; wires that end beside it: adder_16_bit_ic_1_out_4[15], adder_16_bit_ic_1_out_4[15], dip_7408_1_p9, output_sign
  xor_16_line_ic xor_16_line_ic_3 (
    .input_1(adder_16_bit_ic_1_out_4), .input_2(bit_extender_3_out), .\output (xor_16_line_ic_3_output));
  adder_16_bit_ic adder_16_bit_ic_2 (
    .input_1({16{1'b0}}), .input_2(xor_16_line_ic_3_output), .Cin(adder_16_bit_ic_1_out_4[15]),
    .out_4(\output ));  // open: out_5
endmodule

// 7486 xor (4 ic)
module xor_16_line_ic (
  input  [15:0] input_1,
  input  [15:0] input_2,
  output [15:0] \output 
);

  // DIP_7486 dip_7486_1: pin names not known; wires that end beside it: input_1[0], input_2[0], \output [0], input_1[1], input_2[1], \output [1], input_2[3], input_1[3], \output [3], input_2[2], input_1[2]
  // DIP_7486 dip_7486_2: pin names not known; wires that end beside it: input_1[4], input_2[4], \output [4], input_1[5], input_2[5], \output [5], \output [2], input_2[7], input_1[7], \output [7], input_2[6], input_1[6], \output [6]
  // DIP_7486 dip_7486_3: pin names not known; wires that end beside it: input_1[8], input_2[8], \output [8], input_1[9], input_2[9], \output [9], input_2[11], input_1[11], \output [11], input_2[10], input_1[10]
  // DIP_7486 dip_7486_4: pin names not known; wires that end beside it: input_1[12], input_2[12], \output [12], input_1[13], input_2[13], \output [13], \output [10], input_2[15], input_1[15], \output [15], input_2[14], input_1[14], \output [14]

  // Other names for the same wires on the sheet: A1 = input_1[0]; A2 = input_1[1]; A3 = input_1[2]; A4 = input_1[3];
  //   A5 = input_1[4]; A6 = input_1[5]; A7 = input_1[6]; A8 = input_1[7]; A9 = input_1[8]; A10 = input_1[9];
  //   A11 = input_1[10]; A12 = input_1[11]; A13 = input_1[12]; A14 = input_1[13]; A15 = input_1[14];
  //   A16 = input_1[15]; B1 = input_2[0]; B2 = input_2[1]; B3 = input_2[2]; B4 = input_2[3]; B5 = input_2[4];
  //   B6 = input_2[5]; B7 = input_2[6]; B8 = input_2[7]; B9 = input_2[8]; B10 = input_2[9]; B11 = input_2[10];
  //   B12 = input_2[11]; B13 = input_2[12]; B14 = input_2[13]; B15 = input_2[14]; B16 = input_2[15]
endmodule

// 7408 and (4 ic)
module and_16_line_ic (
  input  [15:0] input_1,
  input  [15:0] input_2,
  output [15:0] \output 
);

  // DIP_7408 dip_7408_1: pin names not known; wires that end beside it: input_1[0], input_2[0], \output [0], input_1[1], input_2[1], \output [1], input_2[3], input_1[3], \output [3], input_2[2], input_1[2], \output [2]
  // DIP_7408 dip_7408_2: pin names not known; wires that end beside it: input_1[4], input_2[4], \output [4], input_1[5], input_2[5], \output [5], input_2[7], input_1[7], \output [7], input_2[6], input_1[6], \output [6]
  // DIP_7408 dip_7408_3: pin names not known; wires that end beside it: input_1[8], input_2[8], \output [8], input_1[9], input_2[9], \output [9], input_2[11], input_1[11], \output [11], input_2[10], input_1[10]
  // DIP_7408 dip_7408_4: pin names not known; wires that end beside it: input_1[12], input_2[12], \output [12], input_1[13], input_2[13], \output [13], \output [10], input_2[15], input_1[15], \output [15], input_2[14], input_1[14], \output [14]

  // Other names for the same wires on the sheet: A1 = input_1[0]; A2 = input_1[1]; A3 = input_1[2]; A4 = input_1[3];
  //   A5 = input_1[4]; A6 = input_1[5]; A7 = input_1[6]; A8 = input_1[7]; A9 = input_1[8]; A10 = input_1[9];
  //   A11 = input_1[10]; A12 = input_1[11]; A13 = input_1[12]; A14 = input_1[13]; A15 = input_1[14];
  //   A16 = input_1[15]; B1 = input_2[0]; B2 = input_2[1]; B3 = input_2[2]; B4 = input_2[3]; B5 = input_2[4];
  //   B6 = input_2[5]; B7 = input_2[6]; B8 = input_2[7]; B9 = input_2[8]; B10 = input_2[9]; B11 = input_2[10];
  //   B12 = input_2[11]; B13 = input_2[12]; B14 = input_2[13]; B15 = input_2[14]; B16 = input_2[15]
endmodule

// adder (4 ic)
module adder_16_bit_ic (
  input  Cin,
  input  [15:0] input_1,
  input  [15:0] input_2,
  output [15:0] out_4,
  output out_5
);

  wire dip_74283_2_p7, dip_74283_3_p7, dip_74283_4_p7;

  // DIP_74283 dip_74283_1: pin names not known; wires that end beside it: out_4[1], input_1[1], input_2[1], out_4[0], input_1[0], input_2[0], Cin, input_2[2], input_1[2], out_4[2], input_2[3], input_1[3], out_4[3]
  // DIP_74283 dip_74283_2: pin names not known; wires that end beside it: out_4[5], input_1[5], input_2[5], out_4[4], input_1[4], input_2[4], dip_74283_2_p7, dip_74283_2_p7, input_2[6], input_1[6], out_4[6], input_2[7], input_1[7], out_4[7]
  // DIP_74283 dip_74283_3: pin names not known; wires that end beside it: out_4[9], input_1[9], input_2[9], out_4[8], input_1[8], input_2[8], dip_74283_3_p7, dip_74283_3_p7, input_2[10], input_1[10], out_4[10], input_2[11], input_1[11], out_4[11]
  // DIP_74283 dip_74283_4: pin names not known; wires that end beside it: out_4[13], input_1[13], input_2[13], out_4[12], input_1[12], input_2[12], dip_74283_4_p7, dip_74283_4_p7, input_2[14], input_1[14], out_4[14], input_2[15], input_1[15], out_4[15], out_5

  // Other names for the same wires on the sheet: A1 = input_1[0]; A2 = input_1[1]; A3 = input_1[2]; A4 = input_1[3];
  //   A5 = input_1[4]; A6 = input_1[5]; A7 = input_1[6]; A8 = input_1[7]; A9 = input_1[8]; A10 = input_1[9];
  //   A11 = input_1[10]; A12 = input_1[11]; A13 = input_1[12]; A14 = input_1[13]; A15 = input_1[14];
  //   A16 = input_1[15]; B1 = input_2[0]; B2 = input_2[1]; B3 = input_2[2]; B4 = input_2[3]; B5 = input_2[4];
  //   B6 = input_2[5]; B7 = input_2[6]; B8 = input_2[7]; B9 = input_2[8]; B10 = input_2[9]; B11 = input_2[10];
  //   B12 = input_2[11]; B13 = input_2[12]; B14 = input_2[13]; B15 = input_2[14]; B16 = input_2[15]
endmodule

// +
module adder_4_bit_ic (
  input  [3:0] input_1,
  input  Cin,
  input  [3:0] input_2,
  output [3:0] out_4,
  output out_5
);

  // DIP_74283 dip_74283_1: pin names not known; wires that end beside it: out_4[1], input_1[1], input_2[1], out_4[0], input_1[0], input_2[0], Cin, input_2[2], input_1[2], out_4[2], input_2[3], input_1[3], out_4[3], out_5

  // Other names for the same wires on the sheet: A1 = input_1[0]; A2 = input_1[1]; A3 = input_1[2]; A4 = input_1[3];
  //   B1 = input_2[0]; B2 = input_2[1]; B3 = input_2[2]; B4 = input_2[3]
endmodule

module demo_ic (
  input  [15:0] in_1,
  input  [15:0] in_2,
  output [15:0] out_3,
  output underflow,
  output overflow
);

  final_circuit_ic final_circuit_ic_1 (
    .input_fp_1(in_1), .input_fp_2(in_2), .sum(out_3), .underflow(underflow), .overflow(overflow));
endmodule
