// Digital circuit ALU8bit.dig as structural Verilog
module ALU8bit (
  input  S_0,
  input  S_1,
  input  S_2,
  input  C_in,
  input  [7:0] A,
  input  [7:0] B,
  output C_out,
  output OF,
  output ZF,
  output [7:0] Z
);

  wire U0_p1, U0_p15;

  // _74382 U0: pin names not known; wires that end beside it: U0_p1, B[0], A[0], B[1], A[1], B[2], A[2], B[3], A[3], S_0, S_1, S_2, 1'b1, 1'b0, U0_p15, Z[0], Z[1], Z[2], Z[3]
  // _74382 U1: pin names not known; wires that end beside it: U0_p15, B[4], A[4], B[5], A[5], B[6], A[6], B[7], A[7], S_0, S_1, S_2, 1'b1, 1'b0, C_out, OF, Z[4], Z[5], Z[6], Z[7]
  or or_1 (U0_p1, C_in, ~S_1, ~S_0, S_2);  // Or
  nor nor_1 (ZF, Z[0], Z[1], Z[2], Z[3], Z[7], Z[6], Z[5], Z[4]);

  // Notes on the sheet:
  //   74x4078
endmodule
