// Digital circuit FwdUnit.dig as structural Verilog
module FwdUnit (
  input  EX_MEM_RegWrite,
  input  [3:0] EX_MEM_RegRd,
  input  [3:0] ID_EX_RegRs,
  input  [3:0] ID_EX_RegRt,
  input  MEM_WB_RegWrite,
  input  [3:0] MEM_WB_RegRd,
  output FwdA2,
  output FwdA1,
  output FwdB2,
  output FwdB1
);

  wire and_3_out, and_4_out, comparator_1_eq, comparator_2_eq, comparator_3_eq, comparator_4_eq,
       comparator_5_eq, comparator_6_eq;

  Comparator #(.Bits(4)) comparator_1 (.a(4'b0000), .b(EX_MEM_RegRd), .eq(comparator_1_eq));  // open: gt, lt
  Comparator #(.Bits(4)) comparator_2 (.a(EX_MEM_RegRd), .b(ID_EX_RegRs), .eq(comparator_2_eq));  // open: gt, lt
  Comparator #(.Bits(4)) comparator_3 (.a(EX_MEM_RegRd), .b(ID_EX_RegRt), .eq(comparator_3_eq));  // open: gt, lt
  Comparator #(.Bits(4)) comparator_4 (.a(4'b0000), .b(MEM_WB_RegRd), .eq(comparator_4_eq));  // open: gt, lt
  Comparator #(.Bits(4)) comparator_5 (.a(MEM_WB_RegRd), .b(ID_EX_RegRs), .eq(comparator_5_eq));  // open: gt, lt
  Comparator #(.Bits(4)) comparator_6 (.a(MEM_WB_RegRd), .b(ID_EX_RegRt), .eq(comparator_6_eq));  // open: gt, lt
  and and_1 (FwdA2, EX_MEM_RegWrite, ~comparator_1_eq, comparator_2_eq);  // And
  and and_2 (FwdB2, EX_MEM_RegWrite, ~comparator_1_eq, comparator_3_eq);  // And
  and and_3 (and_3_out, MEM_WB_RegWrite, ~comparator_4_eq, comparator_5_eq);  // And
  and and_4 (and_4_out, MEM_WB_RegWrite, ~comparator_4_eq, comparator_6_eq);  // And
  and and_5 (FwdA1, ~FwdA2, and_3_out);  // And
  and and_6 (FwdB1, ~FwdB2, and_4_out);  // And
endmodule

/* Code that sets the parameters or builds the circuit:
(1)
*/

/* Code that sets the parameters or builds the circuit:
(2)
*/

/* Code that sets the parameters or builds the circuit:
(3)
*/

/* Code that sets the parameters or builds the circuit:
(4)
*/
