// Digital circuit Registers.dig as structural Verilog
module Registers (
  input  [3:0] RegWSelect,
  input  RegWrite,
  input  [3:0] ReadSelect1,
  input  [3:0] ReadSelect2,
  input  [7:0] WriteData,
  input  CLK,
  output [7:0] Data1,
  output [7:0] Data2,
  output [7:0] t0,
  output [7:0] t1,
  output [7:0] t2,
  output [7:0] t3,
  output [7:0] t4,
  output [7:0] zero
);

  wire _3_to_8_Decoder_p9, _3_to_8_Decoder_p10, _3_to_8_Decoder_p11, _3_to_8_Decoder_p12,
       _3_to_8_Decoder_p13, _3_to_8_Decoder_p14, _3_to_8_Decoder_p15, not_1_out;
  wire [7:0] sp_q, t5_q;

  // _74238 _3_to_8_Decoder: pin names not known; wires that end beside it: RegWSelect[0], RegWSelect[2], RegWSelect[1], RegWrite, 1'b0, 1'b0, 1'b1, 1'b0, _3_to_8_Decoder_p9, _3_to_8_Decoder_p10, _3_to_8_Decoder_p11, _3_to_8_Decoder_p12, _3_to_8_Decoder_p13, _3_to_8_Decoder_p14, _3_to_8_Decoder_p15
  not not_1 (not_1_out, CLK);
  Register #(.Bits(8)) u_zero (.D({8{1'b0}}), .C(not_1_out), .en(1'b0), .Q(zero));
  Register #(.Bits(8)) u_t0 (.D(WriteData), .C(not_1_out), .en(_3_to_8_Decoder_p9), .Q(t0));
  Register #(.Bits(8)) u_t1 (.D(WriteData), .C(not_1_out), .en(_3_to_8_Decoder_p10), .Q(t1));
  Register #(.Bits(8)) u_t2 (.D(WriteData), .C(not_1_out), .en(_3_to_8_Decoder_p11), .Q(t2));
  Register #(.Bits(8)) u_t3 (.D(WriteData), .C(not_1_out), .en(_3_to_8_Decoder_p12), .Q(t3));
  Register #(.Bits(8)) u_t4 (.D(WriteData), .C(not_1_out), .en(_3_to_8_Decoder_p13), .Q(t4));
  Register #(.Bits(8)) t5 (.D(WriteData), .C(not_1_out), .en(_3_to_8_Decoder_p14), .Q(t5_q));
  Register #(.Bits(8)) sp (.D(WriteData), .C(not_1_out), .en(_3_to_8_Decoder_p15), .Q(sp_q));
  Multiplexer #(.Selector_Bits(3), .Bits(8)) multiplexer_1 (
    .sel(ReadSelect1[2:0]), .in_0(zero), .in_1(t0), .in_2(t1), .in_3(t2), .in_4(t3), .in_5(t4), .in_6(t5_q),
    .in_7(sp_q), .out(Data1));
  Multiplexer #(.Selector_Bits(3), .Bits(8)) multiplexer_2 (
    .sel(ReadSelect2[2:0]), .in_0(zero), .in_1(t0), .in_2(t1), .in_3(t2), .in_4(t3), .in_5(t4), .in_6(t5_q),
    .in_7(sp_q), .out(Data2));

  // Other names for the same wires on the sheet: WD[7:0] = WriteData

  // Notes on the sheet:
  //   RegWSelect: pin 1
  //   RegWrite: pin 2
  //   ReadSelect1: pin 3
  //   ReadSelect2: pin 4
  //   Data1: pin 14
  //   Data2: pin 13
  //   zero: pin 7
  //   WriteData: pin 5
  //   CLK: pin 6
endmodule
