// Digital circuit main.dig as structural Verilog
module main (
  input  CLOCK,
  input  ENABLE
);

  wire ALUsrc, ALUSrc_q, clk, EX_MEM_MemRead, EX_MEM_MemWrite, EX_MEM_RegWrite, ID_EX_MemRead,
       ID_EX_MemToReg, ID_EX_MemWrite, ID_EX_RegWrite, Jump, MEM_WB_RegWrite, MemRead, MemToReg,
       MemToReg_2_q, MemToReg_3_q, MemWrite, RegDest, RegDest_q, registers_1_p1, registers_1_p3,
       registers_1_p5, registers_1_p7, registers_1_p9, RegWrite, sbeq, sbneq;
  wire [1:0] undriven_2, undriven_3;
  wire [2:0] ALUop, ALUop_q;
  wire [3:0] EX_MEM_RegRd, ID_EX_RegRd, MEM_WB_RegRd, Rd_q, Rs_q, Rt_q;
  wire [7:0] ALURes, ALURes_2_q, DataMemory_d, EX_MEM_ALURes, FinRes, Imm_q, MemOut_q, MemVal_q,
       multiplexer_2_out, multiplexer_3_out, multiplexer_4_out, PC_q, RD1_q, RD2_q, registers_1_p11,
       registers_1_p13, undriven;
  wire [19:0] IF_ID_q, Instruction_Memory_d;

  not not_1 (clk, CLOCK);
  ALU8bit alu8bit_1 ();
  Register #(.Bits(8)) PC (.D(undriven), .C(clk), .en(ENABLE), .Q(PC_q));
  ROM #(.AddrBits(8), .Bits(20)) Instruction_Memory (.A(PC_q), .sel(1'b1), .D(Instruction_Memory_d));
  Register #(.Bits(20)) IF_ID (.D(Instruction_Memory_d), .C(clk), .en(ENABLE), .Q(IF_ID_q));
  ROM #(.AddrBits(4), .Bits(12)) Control (
    .A(IF_ID_q[19:16]), .sel(1'b1),
    .D({RegDest, Jump, sbneq, sbeq, MemToReg, ALUop, MemWrite, MemRead, ALUsrc, RegWrite}));
  // Probe on registers_1_p1
  // Probe on registers_1_p3
  // Probe on registers_1_p5
  // Probe on registers_1_p7
  // Probe on registers_1_p9
  // Registers registers_1: pin names not known; wires that end beside it: registers_1_p1, clk, registers_1_p3, FinRes, registers_1_p5, IF_ID_q[11:8], registers_1_p7, IF_ID_q[15:12], registers_1_p9, MEM_WB_RegWrite, registers_1_p11, MEM_WB_RegRd, registers_1_p13
  Register u_RegWrite (.D(RegWrite), .C(clk), .en(1'b1), .Q(ID_EX_RegWrite));
  Register u_RegDest (.D(RegDest), .C(clk), .en(1'b1), .Q(RegDest_q));
  Register u_MemWrite (.D(MemWrite), .C(clk), .en(1'b1), .Q(ID_EX_MemWrite));
  Register u_MemRead (.D(MemRead), .C(clk), .en(1'b1), .Q(ID_EX_MemRead));
  Register #(.Bits(4)) Rs (.D(IF_ID_q[15:12]), .C(clk), .en(1'b1), .Q(Rs_q));
  Register #(.Bits(4)) Rt (.D(IF_ID_q[11:8]), .C(clk), .en(1'b1), .Q(Rt_q));
  Register #(.Bits(4)) Rd (.D(IF_ID_q[7:4]), .C(clk), .en(1'b1), .Q(Rd_q));
  Register #(.Bits(8)) RD1 (.D(registers_1_p13), .C(clk), .en(1'b1), .Q(RD1_q));
  Register #(.Bits(8)) RD2 (.D(registers_1_p11), .C(clk), .en(1'b1), .Q(RD2_q));
  Register #(.Bits(8)) Imm (.D(IF_ID_q[7:0]), .C(clk), .en(1'b1), .Q(Imm_q));
  Register u_ALUSrc (.D(ALUsrc), .C(clk), .en(1'b1), .Q(ALUSrc_q));
  Register #(.Bits(3)) u_ALUop (.D(ALUop), .C(clk), .en(1'b1), .Q(ALUop_q));
  Register u_MemToReg (.D(MemToReg), .C(clk), .en(1'b1), .Q(ID_EX_MemToReg));
  Multiplexer #(.Bits(4)) multiplexer_1 (.sel(RegDest_q), .in_0(Rt_q), .in_1(Rd_q), .out(ID_EX_RegRd));
  FwdUnit fwdunit_1 ();
  Multiplexer #(.Selector_Bits(2), .Bits(8)) multiplexer_2 (
    .sel(undriven_3), .in_0(RD1_q), .in_1(FinRes), .in_2(EX_MEM_ALURes), .in_3(EX_MEM_ALURes),
    .out(multiplexer_2_out));
  Multiplexer #(.Selector_Bits(2), .Bits(8)) multiplexer_3 (
    .sel(undriven_2), .in_0(RD2_q), .in_1(FinRes), .in_2(EX_MEM_ALURes), .in_3(EX_MEM_ALURes),
    .out(multiplexer_3_out));
  Multiplexer #(.Bits(8)) multiplexer_4 (
    .sel(ALUSrc_q), .in_0(multiplexer_3_out), .in_1(Imm_q), .out(multiplexer_4_out));
  ALU8bit alu8bit_2 ();
  Register RegWrite_2 (.D(ID_EX_RegWrite), .C(clk), .en(1'b1), .Q(EX_MEM_RegWrite));
  Register MemWrite_2 (.D(ID_EX_MemWrite), .C(clk), .en(1'b1), .Q(EX_MEM_MemWrite));
  Register MemRead_2 (.D(ID_EX_MemRead), .C(clk), .en(1'b1), .Q(EX_MEM_MemRead));
  Register #(.Bits(4)) Rd_2 (.D(ID_EX_RegRd), .C(clk), .en(1'b1), .Q(EX_MEM_RegRd));
  Register #(.Bits(8)) u_ALURes (.D(ALURes), .C(clk), .en(1'b1), .Q(EX_MEM_ALURes));
  Register #(.Bits(8)) MemVal (.D(multiplexer_4_out), .C(clk), .en(1'b1), .Q(MemVal_q));
  Register MemToReg_2 (.D(ID_EX_MemToReg), .C(clk), .en(1'b1), .Q(MemToReg_2_q));
  RAMDualPort #(.AddrBits(8), .Bits(8)) DataMemory (
    .A(EX_MEM_ALURes), .Din(MemVal_q), .str(EX_MEM_MemWrite), .C(clk), .ld(EX_MEM_MemRead), .D(DataMemory_d));
  Register #(.Bits(4)) Rd_3 (.D(EX_MEM_RegRd), .C(clk), .en(1'b1), .Q(MEM_WB_RegRd));
  Register RegWrite_3 (.D(EX_MEM_RegWrite), .C(clk), .en(1'b1), .Q(MEM_WB_RegWrite));
  Register #(.Bits(8)) MemOut (.D(DataMemory_d), .C(clk), .en(1'b1), .Q(MemOut_q));
  Register #(.Bits(8)) ALURes_2 (.D(EX_MEM_ALURes), .C(clk), .en(1'b1), .Q(ALURes_2_q));
  Register MemToReg_3 (.D(MemToReg_2_q), .C(clk), .en(1'b1), .Q(MemToReg_3_q));
  Multiplexer #(.Bits(8)) multiplexer_5 (.sel(MemToReg_3_q), .in_0(ALURes_2_q), .in_1(MemOut_q), .out(FinRes));

  // Notes on the sheet:
  //   CLOCK: Hz: 1048576000
  //   contents of Instruction_Memory (hex, n*v repeats v):
  //   10305,10503,83510,95310,c3510,b3510
  //   IF/ID
  //   contents of Control (hex, n*v repeats v):
  //   63,33,841,220,853,110,53,23,831,821,863,851,861,d6,db,430
  //   ID/EX
  //   EX/MEM
  //   MEM/WB
endmodule
